# Fritzing sketch SalHum (saved by Fritzing 0.9.3b)
breadboards: 1

parts:
  Capacitive_Soil_Moisture_Sensor1 = DFRobot Capacitive Soil Moisture Sensor V1.0 [part_number=SEN0193]
  Componente1 = Adafruit ADS1115 16Bit I2C ADC [part_number="Adafruit #1085"]
  Componente2 = SparkFun ESP8266 Thing
  R1 = Resistor [tolerance=±5% resistance=220 package=THT]

nets:
  N1: Capacitive_Soil_Moisture_Sensor1.A, Componente1.AIN0
  N2: Capacitive_Soil_Moisture_Sensor1.VCC, Componente2.USBVCC
  GND: Capacitive_Soil_Moisture_Sensor1.GND, Componente1.ADDR, Componente2.GND, R1.Pin_1
  N3: Componente1.AIN1, R1.Pin_0
  N4: Componente1.SDA, Componente2.GPIO2
  N5: Componente1.SCL, Componente2.GPIO14

custom parts:
  DFRobot Capacitive Soil Moisture Sensor V1.0: DFRobot Capacitive Soil Moisture Sensor V1.0 This product measures soil moisture levels by capacitive sensing, rather than resistive sensing like other types of moisture sensor. It is made of a corrosion resistant material giving it a long service life. Insert it into soil and impress your friends with the real-time soil moisture data! The product includes an on-board voltage regulator which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
  Adafruit ADS1115 16Bit I2C ADC: For microcontrollers without an analog-to-digital converter or when you want a higher-precision ADC, the ADS1115 provides 16-bit precision at 860 samples/second over I2C. The chip can be configured as 4 single-ended input channels, or two differential channels. As a nice bonus, it even includes a programmable gain amplifier, up to x16, to help boost up smaller single/differential signals to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
