# Fritzing sketch Acelerometro (saved by Fritzing 0.9.3b)
breadboards: 1

parts:
  M1 = gy9250
  Componente1 = SparkFun ESP8266 Thing

nets:
  N1: M1.pin1, Componente1.USBVCC
  N2: M1.pin2, Componente1.GND
  N3: M1.pin3, Componente1.GPIO14
  N4: M1.pin4, Componente1.GPIO2

custom parts:
  gy9250: MPU-9250 module (three-axis gyroscope + three-axis acceleration + three-axis magnetic field). The generic model from ebay et. al. rather than the Sparkfun version.
