# Fritzing sketch General (saved by Fritzing 0.9.3b)
breadboards: 1

parts:
  Capacitive_Soil_Moisture_Sensor1 = DFRobot Capacitive Soil Moisture Sensor V1.0 [part_number=SEN0193]
  Componente1 = Adafruit ADS1115 16Bit I2C ADC [part_number="Adafruit #1085"]
  Componente2 = SparkFun ESP8266 Thing
  R2 = Resistor [tolerance=±5% resistance=2.2k package=THT]
  R3 = Temperature Sensor (Thermistor) [thermistor_type=NTC package=THT]
  R1 = Resistor [tolerance=±5% resistance=10k package=THT]
  M2 = gy9250
  P2 = S1133 Si Photodiode [package="8mm Ceramic [THT]"]
  U2 = IC, SIP package, 4 pins [chip_label=IC]
  R5 = Resistor [tolerance=±5% resistance=220 package=THT]  # not connected
  R6 = Resistor [tolerance=±5% resistance=220 package=THT]  # not connected
  R7 = Resistor [tolerance=±5% resistance=220 package=THT]  # not connected
  R4 = Resistor [tolerance=±5% resistance=220 package=THT]

nets:
  N1: Capacitive_Soil_Moisture_Sensor1.A, Componente1.AIN0
  VCC: Capacitive_Soil_Moisture_Sensor1.VCC, Componente1.AIN3, Componente1.VDD, Componente2.USBVCC, M2.pin1, U2.pin1, R4.Pin_1
  GND: Capacitive_Soil_Moisture_Sensor1.GND, Componente1.ADDR, Componente1.GND, Componente2.GND, R2.Pin_1, R1.Pin_1, M2.pin2, P2.anode, U2.pin3, U2.pin4
  N2: Componente1.AIN2, R3.pin_0
  N3: Componente1.AIN1, R1.Pin_0
  N4: Componente1.SDA, Componente2.GPIO2, M2.pin4
  N5: Componente1.SCL, Componente2.GPIO14, M2.pin3
  N6: Componente2.VCC, R2.Pin_0, R3.pin_1
  N7: P2.cathode, U2.pin2, R4.Pin_0

custom parts:
  DFRobot Capacitive Soil Moisture Sensor V1.0: DFRobot Capacitive Soil Moisture Sensor V1.0 This product measures soil moisture levels by capacitive sensing, rather than resistive sensing like other types of moisture sensor. It is made of a corrosion resistant material giving it a long service life. Insert it into soil and impress your friends with the real-time soil moisture data! The product includes an on-board voltage regulator which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
  Adafruit ADS1115 16Bit I2C ADC: For microcontrollers without an analog-to-digital converter or when you want a higher-precision ADC, the ADS1115 provides 16-bit precision at 860 samples/second over I2C. The chip can be configured as 4 single-ended input channels, or two differential channels. As a nice bonus, it even includes a programmable gain amplifier, up to x16, to help boost up smaller single/differential signals to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
  gy9250: MPU-9250 module (three-axis gyroscope + three-axis acceleration + three-axis magnetic field). The generic model from ebay et. al. rather than the Sparkfun version.
