# Fritzing sketch Fotodiodo (saved by Fritzing 0.9.3b)
breadboards: 1

parts:
  Componente1 = SparkFun ESP8266 Thing
  R1 = Resistor [tolerance=±5% resistance=220 package=THT]
  P1 = S1133 Si Photodiode [package="8mm Ceramic [THT]"]
  U1 = IC, SIP package, 4 pins [chip_label=IC]
  Componente2 = Adafruit ADS1115 16Bit I2C ADC [part_number="Adafruit #1085"]

nets:
  N1: Componente1.GND, R1.Pin_0, P1.cathode, P1.anode, U1.pin2, U1.pin3, U1.pin4
  N2: Componente1.ADC, Componente2.AIN3
  N3: R1.Pin_1, U1.pin1, Componente2.AIN1

custom parts:
  Adafruit ADS1115 16Bit I2C ADC: For microcontrollers without an analog-to-digital converter or when you want a higher-precision ADC, the ADS1115 provides 16-bit precision at 860 samples/second over I2C. The chip can be configured as 4 single-ended input channels, or two differential channels. As a nice bonus, it even includes a programmable gain amplifier, up to x16, to help boost up smaller single/differential signals to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
